# Fritzing sketch Receiver (saved by Fritzing 0.9.2b)
circuit board: 9.68913cm x 7.82421cm
breadboards: 1

parts:
  U1 = ATmega644 [package=pdpi]
  XTAL1 = Crystal [frequency="16 Mhz" package=THT]
  C1 = Ceramic Capacitor [capacitance=100nF package="100 mil [THT, multilayer]"]
  C2 = Ceramic Capacitor [capacitance=100nF package="100 mil [THT, multilayer]"]
  C3 = Electrolytic Capacitor [capacitance=1µF package="100 mil [THT, electrolytic]"]
  S1 = Pushbutton [package=THT]
  R1 = Resistor [tolerance=±5% resistance=220 package=THT]
  IC1 = FRM010 [package=THT]
  R2 = Resistor [tolerance=±5% resistance=220 package=THT]
  J1 = female pin header, 4 pins [form="♀ (female)"]
  Power_plug1 = Power plug
  S2 = Toggle Switch [package=THT]
  S3 = Toggle Switch [package=THT]
  IC2 = Voltage Regulator [package=to-220-alt]
  J2 = female pin header, 4 pins [form="♀ (female)"]
  LED1 = LED - 3mm [color="Red (633nm)" package="3 mm [THT]"]
  Q1 = NPN-Transistor [package="TO92 [THT]"]
  R3 = Resistor [tolerance=±5% resistance=220 package=THT]
  R4 = Resistor [tolerance=±5% resistance=220 package=THT]
  R5 = Resistor [tolerance=±5% resistance=220 package=THT]
  LED2 = LED - 3mm [color="Red (633nm)" package="3 mm [THT]"]
  IC3 = IC, DIP package, 16 pins [chip_label=IC]
  J3 = screw terminal, 2 pins
  J4 = screw terminal, 2 pins
  R6 = Resistor [tolerance=±5% resistance=220 package=THT]

nets:
  N1: U1.PB0, IC1.JP1_-_Welcome_Message_selection
  N2: U1.PB1, IC1.JP2_-_Baud_Rate_selection
  N3: U1.PB2, IC1.JP3_-_Polarity_selection
  N4: U1.PB3, IC1.JP4_-_Number_of_Lines_selection
  N5: U1.RESET, C3.+, S1.leg1, R1.Pin_0
  N6: U1.XTAL2, Q1.E, R4.Pin_0
  N7: U1.PD4, XTAL1.pin_0, C1.0
  N8: U1.PD5, XTAL1.pin_1, C2.0
  GND: U1.PD6, C1.1, C2.1, R1.Pin_1, IC1.LCD_RS, IC1.LCD_E, IC1.Serial_In, IC1.Reset, IC1.0V, IC1.LCD_D4, IC1.LCD_D5, IC1.LCD_D6, IC1.LCD_D7, J1.pin2, J1.pin3, Power_plug1.GND, IC2.GND, J2.pin1, Q1.C, LED2.cathode, IC3.pin4, IC3.pin5, IC3.pin12, IC3.pin13
  N9: U1.GND, U1.PA0, C3.-, S1.leg0, IC1.LCD_PWR, J1.pin4, IC2.OUT, J2.pin4, R4.Pin_1, R5.Pin_1, IC3.pin1, IC3.pin9, IC3.pin16
  N10: U1.PA4, IC3.pin15
  N11: U1.PA3, IC3.pin10
  N12: U1.PA2, IC3.pin7
  N13: U1.PA1, IC3.pin2
  N14: IC1.+V, J2.pin2
  N15: IC1.XTAL#14, R2.Pin_0
  N16: IC1.XTAL#15, R6.Pin_1
  N17: IC1.LED, R3.Pin_1
  N18: R2.Pin_1, R6.Pin_0
  N19: Power_plug1.VCC, S2.L1
  N20: S2.COM, S3.COM, IC2.IN, IC3.pin8
  N21: LED1.cathode, Q1.B
  N22: LED1.anode, R3.Pin_0
  N23: R5.Pin_0, LED2.anode
  N24: IC3.pin3, J4.pin1
  N25: IC3.pin6, J4.pin2
  N26: IC3.pin11, J3.pin2
  N27: IC3.pin14, J3.pin1

notes:
  Receiver
