# Fritzing sketch Transmitter (saved by Fritzing 0.9.2b)
circuit board: 7.29211cm x 7.6063cm
breadboards: 1

parts:
  U1 = ATmega644 [package=pdpi]
  XTAL1 = Crystal [frequency="16 Mhz" package=THT]
  C1 = Ceramic Capacitor [capacitance=100nF package="100 mil [THT, multilayer]"]
  C2 = Ceramic Capacitor [capacitance=100nF package="100 mil [THT, multilayer]"]
  C3 = Electrolytic Capacitor [capacitance=1µF package="100 mil [THT, electrolytic]"]
  S1 = Pushbutton [package=THT]
  R1 = Resistor [tolerance=±5% resistance=220 package=THT]
  IC1 = FRM010 [package=THT]
  X1 = DB9 Connector [package=db9]
  U2 = RS232 Transceiver [package=dil16]
  C4 = Electrolytic Capacitor [capacitance=1µF package="100 mil [THT, electrolytic]"]
  C5 = Electrolytic Capacitor [capacitance=1µF package="100 mil [THT, electrolytic]"]
  C6 = Electrolytic Capacitor [capacitance=1µF package="100 mil [THT, electrolytic]"]
  C7 = Electrolytic Capacitor [capacitance=1µF package="100 mil [THT, electrolytic]"]
  R2 = Resistor [tolerance=±5% resistance=220 package=THT]
  J1 = female pin header, 4 pins [form="♀ (female)"]
  Power_plug1 = Power plug
  S2 = Toggle Switch [package=THT]
  S3 = Toggle Switch [package=THT]
  IC2 = Voltage Regulator [package=to-220-alt]
  R6 = Resistor [tolerance=±5% resistance=220 package=THT]
  LED3 = LED - 3mm [color="Red (633nm)" package="3 mm [THT]"]

nets:
  N1: U1.PB0, IC1.JP1_-_Welcome_Message_selection
  N2: U1.PB1, IC1.JP2_-_Baud_Rate_selection
  N3: U1.PB2, IC1.JP3_-_Polarity_selection
  N4: U1.PB3, IC1.JP4_-_Number_of_Lines_selection
  N5: U1.PB4, IC1.+V
  N6: U1.RESET, C3.+, S1.leg1, R1.Pin_0
  N7: U1.VCC, U2.R1OUT
  N8: U1.GND#10, U2.T1IN
  N9: U1.PD4, XTAL1.pin_0, C1.0
  N10: U1.PD5, XTAL1.pin_1, C2.0
  GND: U1.PD6, C1.1, C2.1, R1.Pin_1, IC1.LCD_RS, IC1.LCD_E, IC1.Serial_In, IC1.Reset, IC1.0V, IC1.LCD_D4, IC1.LCD_D5, IC1.LCD_D6, IC1.LCD_D7, X1.5, U2.GND, C6.+, J1.pin1, Power_plug1.GND, IC2.GND, LED3.cathode
  N11: U1.GND#30, U1.PA0, IC1.LCD_PWR, J1.pin3, IC2.OUT, R6.Pin_1
  N12: C3.-, S1.leg0, U2.VCC, C7.-
  N13: IC1.XTAL#14, R2.Pin_0
  N14: IC1.XTAL#15, R2.Pin_1
  N15: IC1.LED, J1.pin2
  N16: X1.2, U2.T1OUT
  N17: X1.3, U2.R1IN
  N18: U2.C1+, C4.+
  N19: U2.V+, C7.+
  N20: U2.C1-, C4.-
  N21: U2.C2+, C5.+
  N22: U2.C2-, C5.-
  N23: U2.V-, C6.-
  N24: Power_plug1.VCC, S2.L1
  N25: S2.COM, S3.COM, IC2.IN
  N26: R6.Pin_0, LED3.anode

notes:
  Transmitter
